// Logisim project dpa-logisim buffer.circ as structural Verilog: 1 circuit, main circuit main
module main (
  input  [3:0] Address,
  input  in_2,
  input  Clear,
  input  in_4,
  input  Sel,
  input  in_6,
  input  in_7,
  input  in_8,
  input  Enable2,
  input  in_10,
  input  in_11,
  input  Enable1,
  input  [3:0] in_13,
  input  in_14,
  input  Load,
  input  [3:0] in_16,
  input  [3:0] Sel_2,
  input  Count,
  input  in_19,
  input  Clear_2,
  input  in_21,
  input  in_22,
  input  [3:0] in_23,
  input  in_24,
  output [3:0] Instruction_Reg,
  output [3:0] Data_Reg1,
  output [3:0] out_27,
  output [3:0] out_28,
  output [3:0] OUTPUT,
  output [3:0] out_30
);

  wire clock_1_out, clock_2_out, clock_3_out;
  wire [3:0] adder_1_out, Buffer2_out, controlled_buffer_1_out, controlled_buffer_2_out, multiplexer_1_out,
       multiplexer_2_out, subtractor_1_out;

  assign Buffer2_out = in_8 ? controlled_buffer_1_out : 4'bz;  // Controlled_Buffer Buffer2
  Clock clock_1 (.out(clock_1_out));
  Register #(.width(4)) register_1 (.D(Buffer2_out), .en(in_6), .Q(Instruction_Reg), .clk(clock_1_out), .clr(in_4));
  Register #(.width(4)) register_2 (
    .D(controlled_buffer_1_out), .en(Enable2), .Q(Data_Reg1), .clk(clock_2_out), .clr(in_10));
  Register #(.width(4)) register_3 (
    .D(controlled_buffer_1_out), .en(Enable1), .Q(out_28), .clk(clock_2_out), .clr(in_14));
  Counter #(.width(4), .max('hf)) counter_1 (
    .load(Load), .D(in_16), .count(Count), .Q(out_30), .clk(clock_2_out), .clr(Clear_2));  // open: carry
  Clock clock_2 (.out(clock_2_out));
  Multiplexer #(.select(4), .width(4)) multiplexer_1 (
    .in0(out_28), .in1(out_30), .out(multiplexer_1_out), .sel(Sel_2));  // open: in2, in3, in4, in5, in6, in7, in8, in9, in10, in11, in12, in13, in14, in15, en
  Adder #(.width(4)) adder_1 (.a(Data_Reg1), .b(multiplexer_1_out), .out(adder_1_out));  // open: cin, cout
  Subtractor #(.width(4)) subtractor_1 (
    .a(Data_Reg1), .b(multiplexer_1_out), .out(subtractor_1_out));  // open: bin, bout
  Multiplexer #(.width(4), .enable("false")) multiplexer_2 (
    .in0(Instruction_Reg), .in1(in_23), .out(multiplexer_2_out), .sel(in_19));
  Multiplexer #(.select(4), .width(4), .enable("false")) multiplexer_3 (
    .in1(adder_1_out), .in2(subtractor_1_out), .in3(multiplexer_1_out), .out(in_13), .sel(multiplexer_2_out));  // open: in0, in4, in5, in6, in7, in8, in9, in10, in11, in12, in13, in14, in15
  assign Address = in_2 ? in_13 : 4'bz;  // Controlled_Buffer Buffer1
  Multiplexer #(.width(4)) multiplexer_4 (.in0(out_27), .in1(in_13), .out(OUTPUT), .sel(in_11));  // open: en
  assign controlled_buffer_1_out = in_24 ? OUTPUT : 4'bz;  // Controlled_Buffer controlled_buffer_1
  Clock clock_3 (.out(clock_3_out));
  assign controlled_buffer_2_out = in_21 ? OUTPUT : 4'bz;  // Controlled_Buffer controlled_buffer_2
  RAM #(.addrWidth(4), .dataWidth(4)) ram_1 (
    .addr(Address), .data(out_27), .sel(Sel), .clk(clock_3_out), .ld(in_7), .clr(Clear));
  ROM #(.addrWidth(4), .dataWidth(4)) rom_1 (
    .addr(controlled_buffer_2_out), .data(controlled_buffer_1_out), .sel(in_22));

  // Notes on the sheet:
  //   clk
  //   Program Counter
  //          Data Reg2
  //                                                     DATA PATH ARCHITECTURE
  //             ALU
  //   a
  //    b
  //   a
  //   Add
  //         Sub
  //   b
  //               ALU Out
  //       RAM
  //   CLk
  //       Load
  //   Instruction Memory
  //   Data Memory
  //   contents of rom_1 (hex, n*v repeats v):
  //   4*0 4 6 6
endmodule
