// Logisim project ALU WITH MUX.circ as structural Verilog: 1 circuit, main circuit main
module main (
  input  in_1,
  input  in_2,
  input  in_3,
  input  in_4,
  input  in_5,
  input  in_6,
  input  in_7,
  input  in_8,
  input  in_9,
  input  in_10,
  output out_11,
  output out_12
);

  wire and_1_out, and_3_out, and_4_out, and_5_out, and_6_out, not_1_out, not_2_out, or_1_out, xor_1_out,
       xor_2_out;

  not not_1 (not_1_out, in_1);
  not not_2 (not_2_out, in_2);
  and and_1 (and_1_out, in_3, in_4);
  or or_1 (or_1_out, in_5, in_6);
  xor xor_1 (xor_1_out, in_7, in_8);
  and and_2 (out_12, in_9, in_10);
  xor xor_2 (xor_2_out, in_9, in_10);
  and and_3 (and_3_out, not_2_out, not_1_out, and_1_out);
  and and_4 (and_4_out, not_1_out, in_2, or_1_out);
  and and_5 (and_5_out, not_2_out, in_1, xor_1_out);
  and and_6 (and_6_out, in_1, in_2, xor_2_out);
  or or_2 (out_11, and_3_out, and_4_out, and_5_out, and_6_out);

  // Notes on the sheet:
  //   ALU with MUX
endmodule
