// Logisim project DMUX1.circ as structural Verilog: 1 circuit, main circuit main
module main (
  input  in_1,
  input  in_2,
  input  in_3,
  output out_4,
  output out_5,
  output out_6,
  output out_7
);

  wire not_1_out, not_2_out;

  not not_1 (not_1_out, in_1);
  not not_2 (not_2_out, in_2);
  and and_1 (out_4, not_2_out, not_1_out, in_3);
  and and_2 (out_5, not_2_out, in_1, in_3);
  and and_3 (out_6, in_2, not_1_out, in_3);
  and and_4 (out_7, in_2, in_1, in_3);

  // Notes on the sheet:
  //   DMUX
endmodule
