// Logisim project Adder.circ as structural Verilog: 1 circuit, main circuit main
module main (
  input  A,
  input  in_2,
  input  B,
  input  in_4,
  input  Cin,
  input  in_6,
  input  in_7,
  output out_8,
  output S,
  output out_10,
  output Cout,
  output out_12,
  output out_13
);

  wire and_2_out, and_3_out, nand_1_out, xor_3_out;

  and and_1 (out_10, in_2, in_4);
  xor xor_1 (out_8, in_2, in_4);
  xor xor_2 (out_12, in_6, in_7);
  nand nand_1 (nand_1_out, in_7, in_6);
  not not_1 (out_13, nand_1_out);
  xor xor_3 (xor_3_out, A, B);
  and and_2 (and_2_out, B, A);
  and and_3 (and_3_out, Cin, xor_3_out);
  xor xor_4 (S, xor_3_out, Cin);
  or or_1 (Cout, and_3_out, and_2_out);

  // Notes on the sheet:
  //   HALF ADDER
  //   using NAND
  //   FULL ADDER
endmodule
