// Logisim project Mux.circ as structural Verilog: 1 circuit, main circuit main
module main (
  input  X,
  input  Y,
  input  A,
  input  B,
  input  C,
  input  D,
  output out_7
);

  wire and_1_out, and_2_out, and_3_out, and_4_out, not_1_out, not_2_out;

  not not_1 (not_1_out, X);
  not not_2 (not_2_out, Y);
  and and_1 (and_1_out, not_2_out, not_1_out, A);
  and and_2 (and_2_out, not_1_out, Y, B);
  and and_3 (and_3_out, not_2_out, X, C);
  and and_4 (and_4_out, Y, X, D);
  or or_1 (out_7, and_1_out, and_2_out, and_3_out, and_4_out);

  // Notes on the sheet:
  //   X'Y'A+ X'YB + XY'C+XYD
  //   Mux
endmodule
