// Logisim project ALLTYPESOFGATE.circ as structural Verilog: 1 circuit, main circuit main
module main (
  input  _1_AND_GATE,
  input  in_2,
  input  in_3,
  input  in_4,
  input  in_5,
  input  in_6,
  input  in_7,
  input  in_8,
  input  in_9,
  input  in_10,
  input  in_11,
  input  in_12,
  input  in_13,
  output out_14,
  output out_15,
  output out_16,
  output out_17,
  output out_18,
  output out_19,
  output out_20
);

  and and_1 (out_14, _1_AND_GATE, in_2);
  or or_1 (out_15, in_3, in_4);
  not not_1 (out_16, in_5);
  nand nand_1 (out_17, in_6, in_7);
  nor nor_1 (out_18, in_8, in_9);
  xor xor_1 (out_19, in_10, in_11);
  xnor xnor_1 (out_20, in_12, in_13);

  // Notes on the sheet:
  //   2.OR GATE 
  //   3.NOT
  //   4.NAND GATE 
  //   5.NOR GATE
  //   6.XOR GATE
  //   7.XNOR GATE 
  //   AND GATE (IC 7408)
  //   OR GATE 
endmodule
